# Fritzing sketch FM Radio scheme (saved by Fritzing 0.9.3b)
breadboards: 1

parts:
  IC1 = DIP - 10 pins [chip_label=TA5767 package="DIP (Dual Inline) [THT]"]
  Parça1 = Arduino Uno (Rev3)
  LCD1 = LCD screen
  Ekran = Rotary Potentiometer (Small) [maximum_resistance=100kΩ package=THT]
  Kanal_Switch = Rotary Potentiometer (Small) [maximum_resistance=100kΩ package=THT]

nets:
  N1: IC1.DATA, Parça1.A4/SDA
  N2: IC1.SCLK, Parça1.A5/SCL
  VCC: IC1.VCC, Parça1.5V, LCD1.VDD, LCD1.LED+, Ekran.leg1, Kanal_Switch.leg1
  GND: IC1.GND, Parça1.GND, LCD1.VSS, LCD1.R/W, LCD1.LED-, Ekran.leg2, Kanal_Switch.leg2
  N3: Parça1.A0, Kanal_Switch.wiper
  N4: Parça1.D11_PWM/MOSI, LCD1.E
  N5: Parça1.D12/MISO, LCD1.RS
  N6: Parça1.D2, LCD1.DB7
  N7: Parça1.D3_PWM, LCD1.DB6
  N8: Parça1.D4, LCD1.DB5
  N9: Parça1.D5_PWM, LCD1.DB4
  N10: LCD1.V0, Ekran.wiper

custom parts:
  DIP - 10 pins: A DIP stand-in part for whatever IC you want. With 10 pins on a 300mil dual inline package (DIP) footprint.
