# Fritzing sketch mert's workspace (saved by Fritzing 0.9.3b)
breadboards: 1

parts:
  part = Arduino Uno (Rev3)
  Ekran = LCD screen
  R1_(Ekran_Parlaklık_switch) = Rotary Potentiometer (Small) [maximum_resistance=100kΩ package=THT]
  R2_(Kanal_switch) = Rotary Potentiometer (Small) [maximum_resistance=100kΩ package=THT]
  Radyo_Modülü = DIP - 10 pins [chip_label=TEA5767 package="DIP (Dual Inline) [THT]"]

nets:
  N1: part.A0, R2_(Kanal_switch).wiper
  N2: part.A4/SDA, Radyo_Modülü.DATA
  N3: part.A5/SCL, Radyo_Modülü.SCLK
  N4: part.D11_PWM/MOSI, Ekran.E
  N5: part.D12/MISO, Ekran.RS
  GND: part.GND, Ekran.VSS, Ekran.R/W, Ekran.LED-, R1_(Ekran_Parlaklık_switch).leg2, R2_(Kanal_switch).leg2, Radyo_Modülü.GND
  N6: part.D2, Ekran.DB7
  N7: part.D3_PWM, Ekran.DB6
  N8: part.D4, Ekran.DB5
  N9: part.D5_PWM, Ekran.DB4
  5V: part.5V, Ekran.VDD, Ekran.LED+, R1_(Ekran_Parlaklık_switch).leg1, R2_(Kanal_switch).leg1, Radyo_Modülü.VCC
  N10: Ekran.V0, R1_(Ekran_Parlaklık_switch).wiper

custom parts:
  DIP - 10 pins: A DIP stand-in part for whatever IC you want. With 10 pins on a 300mil dual inline package (DIP) footprint.

// code stored in the sketch: kod.ino
#include <Wire.h>
#include <LiquidCrystal.h>

unsigned char frekansH = 0;
unsigned char frekansL = 0;

unsigned int frekansB;
double frekans = 0;

static char frekans_ekran[15];

LiquidCrystal lcd(12, 11, 5, 4, 3, 2);

void setup()
{
  Wire.begin();
  lcd.begin(16, 2);
  frekans = 93.0;
  frekansAyarla();
  lcd.setCursor(3, 0);
  lcd.print("FM Radyo");
}

void loop()
{
  int reading = analogRead(0);
  frekans = ((double)reading * (108.0 - 87.5)) / 1024.0 + 87.5;
  frekans = ((int)(frekans * 10)) / 10.0;
  frekansAyarla();
  dtostrf(frekans, 6, 2, frekans_ekran);
  lcd.setCursor(4, 1);
  lcd.print(frekans_ekran);
}

void frekansAyarla()
{
  frekansB = 4 * (frekans * 1000000 + 225000) / 32768;
  frekansH = frekansB >> 8;
  frekansL = frekansB & 0XFF;
  delay(100);
  Wire.beginTransmission(0x60);
  Wire.write(frekansH);
  Wire.write(frekansL);
  Wire.write(0xB0);
  Wire.write(0x10);
  Wire.write((byte)0x00);
  Wire.endTransmission();
  delay(100);
}
